# Fritzing sketch servo_control_layout (saved by Fritzing 0.9.3b)
breadboards: 1

parts:
  Part1 = Arduino Uno (Rev3)
  S1 = Pushbutton [package="[THT]"]
  S2 = Pushbutton [package="[THT]"]
  R3 = Resistor [tolerance=±5% resistance=10k package=THT]
  R4 = Resistor [tolerance=±5% resistance=10k package=THT]
  J1 = Basic Servo

nets:
  N1: Part1.D12/MISO, J1.pulse
  GND: Part1.GND, R3.Pin_0, R4.Pin_1, J1.gnd
  5V: Part1.D4, Part1.5V, S1.Pin_3, S1.Pin_4, S2.Pin_4, J1.vcc
  N2: S1.Pin_1, S1.Pin_2, R4.Pin_0
  N3: S2.Pin_1, S2.Pin_2, R3.Pin_1
